# Fritzing sketch electronic (saved by Fritzing 0.7.11b)
breadboards: 2

parts:
  R2 = Resistor [tolerance=±5% resistance=220 package=THT]
  LED6 = LED - 5mm [color="Infrared (940nm)" package="5 mm [THT]"]
  LED7 = LED - 5mm [color="Infrared (940nm)" package="5 mm [THT]"]
  LED8 = LED - 5mm [color="Infrared (850nm)" package="5 mm [THT]"]
  R4 = Resistor [tolerance=±5% resistance=1k package=THT]
  R5 = Resistor [tolerance=±5% resistance=220 package=THT]
  R6 = Resistor [tolerance=±5% resistance=220 package=THT]
  R7 = Resistor [tolerance=±5% resistance=220 package=THT]
  LED9 = LED - 5mm [color="Blue (525nm)" package="5 mm [THT]"]
  LED10 = LED - 5mm [color="Blue (525nm)" package="5 mm [THT]"]
  LED11 = LED - 5mm [color="White (8000K)" package="5 mm [THT]"]
  R3 = Trimmer Potentiometer [package=THT]
  J3 = male pin header, 4 pins [form="♂ (male)"]
  R8 = Resistor [tolerance=±5% resistance=220 package=THT]
  XTAL3 = Crystal [frequency="16 Mhz" package=THT]
  U2 = Voltage Regulator - 5V [package="TO220 [THT]"]
  Part1 = Arduino MicroSD Shield
  C3 = Ceramic Capacitor [capacitance=0.22mF voltage=16V package="200 mil [THT, multilayer]"]
  C2 = Ceramic Capacitor [capacitance=0.22mF voltage=16V package="200 mil [THT, multilayer]"]
  J5 = male pin header, 4 pins [form="♂ (male)"]
  J6 = male pin header, 6 pins [form="♂ (male)"]
  J7 = male pin header, 6 pins [form="♂ (male)"]
  C5 = Electrolytic Capacitor [capacitance=100µF voltage=16V package="100 mil [THT, electrolytic]"]
  C4 = Electrolytic Capacitor [capacitance=100µF voltage=16V package="100 mil [THT, electrolytic]"]
  U1 = atmega328 [package=dip]
  J8 = male pin header, 2 pins [form="♂ (male)"]
  D1 = Rectifier Diode [part_number=1N4001 package="300 mil [THT]"]
  J9 = male pin header, 2 pins [form="♂ (male)"]
  D2 = Rectifier Diode [part_number=1N4001 package="300 mil [THT]"]

nets (from the schematic view):
  N1: R2.Pin_0, U1.D2
  N2: R2.Pin_1, LED6.anode, LED7.anode
  GND: LED6.cathode, LED8.cathode, U2.GND, J5.pin4, J6.pin5, C5.-, C4.-, J9.pin2
  N3: LED8.anode, R3.wiper, R3.leg2, U1.A5
  N4: R4.Pin_0, R8.Pin_1, J6.pin6, U1.VCC, U1.AREF, J8.pin1, D1.cathode
  N5: R4.Pin_1, R3.leg1
  N6: R5.Pin_0, J3.pin2
  N7: R5.Pin_1, LED11.anode
  N8: R6.Pin_0, J3.pin3
  N9: R6.Pin_1, LED10.anode
  N10: R7.Pin_0, J3.pin1
  N11: R7.Pin_1, LED9.anode
  N12: LED9.cathode, LED10.cathode, J3.pin4
  N13: R8.Pin_0, U1.RESET
  N14: XTAL3.pin_0, C3.0, U1.XLAT2
  N15: XTAL3.pin_1, C2.0, U1.GND#7, U1.XLAT1, D2.anode
  7V: U2.input_voltage, C4.+, J9.pin1
  N16: U2.output_voltage, C5.+, D1.anode
  N17: Part1.CS, J7.pin3
  N18: Part1.MOSI, J7.pin4
  N19: Part1.MISO, J7.pin5
  N20: Part1.SCK, J7.pin6
  N21: Part1.5V, J7.pin1
  N22: Part1.GND, J7.pin2
  N23: C3.1, C2.1
  N24: J5.pin1, U1.D5_(PWM)
  N25: J5.pin2, U1.D6_(PWM)
  N26: J5.pin3, U1.D7
  N27: J6.pin1, U1.D13
  N28: J6.pin2, U1.D12
  N29: J6.pin3, U1.D11_(PWM)
  N30: J6.pin4, U1.D8
  N31: J8.pin2, D2.cathode

notes:
  LED8 = Photo diode
  Digital Signal
  Analog Signal
  GND
  VCC
